# Fritzing sketch receiver (saved by Fritzing 0.9.2b)
circuit board: 8.46667cm x 5.64444cm
breadboards: 1

parts:
  RJ45 = RJ45 Jack [package=rj45-8]
  MAX485 = MAX485 [package=dil08]
  R1 = Resistor [tolerance=±5% resistance=120 package=THT]
  R-7850 = Voltage Regulator - 5V [package="TO220 [THT]"]
  R2 = Resistor [tolerance=±5% resistance=470k package=THT]
  R3 = Resistor [tolerance=±5% resistance=470k package=THT]
  LED = Header 3 [package=molex-1x3_lock]

nets:
  N1: RJ45.1, MAX485.A, R1.Pin_0, R3.Pin_1
  N2: RJ45.2, MAX485.B, R1.Pin_1, R2.Pin_1
  GND: RJ45.3, RJ45.5, RJ45.7, MAX485.RE, MAX485.DE, MAX485.GND, R-7850.GND, R3.Pin_0, LED.2
  N3: RJ45.4, RJ45.6, RJ45.8, R-7850.input_voltage
  N4: MAX485.RO, LED.3
  N5: MAX485.VCC, R-7850.output_voltage, R2.Pin_0, LED.1
